# Fritzing sketch origamiThrowie (saved by Fritzing 0.9.3b)
circuit board: 2.5cm x 2.5cm
breadboards: 1

parts:
  R1 = Resistor [tolerance=±5% resistance=220 package=THT]
  NEOPIXEL1 = Neopixel Strip -- White (60/m)
  C1 = Ceramic Capacitor [capacitance=0.1µF package="100 mil [THT, multilayer]"]
  U1 = attiny85 [package=dip]
  BAT3 = Battery Holders [package=battcon_12mm]

nets:
  N1: R1.Pin_0, U1.Pin_6
  N2: R1.Pin_1, NEOPIXEL1.DI
  N3: NEOPIXEL1.+5V, U1.Pin_8, BAT3.+#0
  N4: NEOPIXEL1.GND, C1.1, U1.Pin_4, BAT3.-
  N5: C1.0, BAT3.+#3

custom parts:
  Neopixel Strip -- White (60/m): Neopixel Strip, White, 60 pixels per meter.
  Battery Holders: Battery Holders Various common sizes : AA, AAA, 20mm coin cell and 12mm coin cell.
